// Logisim project 1.circ as structural Verilog: 8 circuits, main circuit main
module main (
  input  in_1,
  input  in_2,
  input  in_3,
  input  in_4,
  input  in_5,
  input  in_6,
  input  in_7,
  input  in_8,
  input  in_9,
  input  in_10,
  input  in_11,
  input  in_12,
  input  in_13,
  input  in_14,
  input  in_15,
  input  in_16,
  output out_17,
  output out_18,
  output out_19,
  output out_20,
  output out_21,
  output out_22,
  output out_23,
  output out_24,
  output out_25
);

  wire summator1bit_1_p_out, summator1bit_2_p_out, summator1bit_3_p_out, summator1bit_4_p_out,
       summator1bit_5_p_out, summator1bit_6_p_out, summator1bit_7_p_out;

  summator1bit summator1bit_1 (.x_1(in_8), .x_2(in_16), .p_in(1'b0), .S(out_25), .p_out(summator1bit_1_p_out));
  summator1bit summator1bit_2 (
    .x_1(in_7), .x_2(in_15), .p_in(summator1bit_1_p_out), .S(out_24), .p_out(summator1bit_2_p_out));
  summator1bit summator1bit_3 (
    .x_1(in_6), .x_2(in_14), .p_in(summator1bit_2_p_out), .S(out_23), .p_out(summator1bit_3_p_out));
  summator1bit summator1bit_4 (
    .x_1(in_5), .x_2(in_13), .p_in(summator1bit_3_p_out), .S(out_22), .p_out(summator1bit_4_p_out));
  summator1bit summator1bit_5 (
    .x_1(in_4), .x_2(in_12), .p_in(summator1bit_4_p_out), .S(out_21), .p_out(summator1bit_5_p_out));
  summator1bit summator1bit_6 (
    .x_1(in_3), .x_2(in_11), .p_in(summator1bit_5_p_out), .S(out_20), .p_out(summator1bit_6_p_out));
  summator1bit summator1bit_7 (
    .x_1(in_2), .x_2(in_10), .p_in(summator1bit_6_p_out), .S(out_19), .p_out(summator1bit_7_p_out));
  summator1bit summator1bit_8 (.x_1(in_1), .x_2(in_9), .p_in(summator1bit_7_p_out), .S(out_18), .p_out(out_17));
endmodule

module summator1bit (
  input  x_1,
  input  x_2,
  input  p_in,
  output S,
  output p_out
);

  wire not_1_out, not_2_out, not_3_out, or_1_out, or_2_out, or_3_out, or_4_out, or_5_out, or_6_out, or_7_out;

  not not_1 (not_1_out, x_1);
  not not_2 (not_2_out, x_2);
  not not_3 (not_3_out, p_in);
  or or_1 (or_1_out, x_1, x_2, p_in);
  or or_2 (or_2_out, x_2, not_1_out, not_3_out);
  or or_3 (or_3_out, x_1, not_2_out, not_3_out);
  or or_4 (or_4_out, p_in, not_2_out, not_1_out);
  or or_5 (or_5_out, p_in, x_1);
  or or_6 (or_6_out, x_2, p_in);
  or or_7 (or_7_out, x_2, x_1);
  and and_1 (S, or_1_out, or_2_out, or_3_out, or_4_out);
  and and_2 (p_out, or_5_out, or_6_out, or_7_out);
endmodule

module converse (
  input  x_4,
  input  x_3,
  input  x_2,
  input  x_1,
  output r_4,
  output r_3,
  output r_2,
  output r_1
);

  myxor myxor_1 (.in_1(x_3), .in_2(x_4), .out_3(r_3));
  myxor myxor_2 (.in_1(x_2), .in_2(r_3), .out_3(r_2));
  myxor myxor_3 (.in_1(x_1), .in_2(r_2), .out_3(r_1));

  assign r_4 = x_4;
endmodule

module myxor (
  input  in_1,
  input  in_2,
  output out_3
);

  wire and_1_out, and_2_out, not_1_out, not_2_out;

  not not_1 (not_1_out, in_2);
  not not_2 (not_2_out, in_1);
  and and_1 (and_1_out, in_1, not_1_out);
  and and_2 (and_2_out, in_2, not_2_out);
  or or_1 (out_3, and_1_out, and_2_out);
endmodule

module summator8bit (
  input  x1_8,
  input  in_2,
  input  in_3,
  input  in_4,
  input  in_5,
  input  in_6,
  input  in_7,
  input  x1_1,
  input  x2_8,
  input  in_10,
  input  in_11,
  input  in_12,
  input  in_13,
  input  in_14,
  input  in_15,
  input  x2_1,
  output p,
  output s_8,
  output out_19,
  output out_20,
  output out_21,
  output out_22,
  output out_23,
  output out_24,
  output s_1
);

  wire summator1bit_1_p_out, summator1bit_2_p_out, summator1bit_3_p_out, summator1bit_4_p_out,
       summator1bit_5_p_out, summator1bit_6_p_out, summator1bit_7_p_out;

  summator1bit summator1bit_1 (.x_1(x1_1), .x_2(x2_1), .p_in(1'b0), .S(s_1), .p_out(summator1bit_1_p_out));
  summator1bit summator1bit_2 (
    .x_1(in_7), .x_2(in_15), .p_in(summator1bit_1_p_out), .S(out_24), .p_out(summator1bit_2_p_out));
  summator1bit summator1bit_3 (
    .x_1(in_6), .x_2(in_14), .p_in(summator1bit_2_p_out), .S(out_23), .p_out(summator1bit_3_p_out));
  summator1bit summator1bit_4 (
    .x_1(in_5), .x_2(in_13), .p_in(summator1bit_3_p_out), .S(out_22), .p_out(summator1bit_4_p_out));
  summator1bit summator1bit_5 (
    .x_1(in_4), .x_2(in_12), .p_in(summator1bit_4_p_out), .S(out_21), .p_out(summator1bit_5_p_out));
  summator1bit summator1bit_6 (
    .x_1(in_3), .x_2(in_11), .p_in(summator1bit_5_p_out), .S(out_20), .p_out(summator1bit_6_p_out));
  summator1bit summator1bit_7 (
    .x_1(in_2), .x_2(in_10), .p_in(summator1bit_6_p_out), .S(out_19), .p_out(summator1bit_7_p_out));
  summator1bit summator1bit_8 (.x_1(x1_8), .x_2(x2_8), .p_in(summator1bit_7_p_out), .S(s_8), .p_out(p));
endmodule

module gray (
  input  in_1,
  input  in_2,
  input  in_3,
  input  in_4,
  input  in_5,
  input  in_6,
  input  in_7,
  input  in_8,
  output out_9,
  output out_10,
  output out_11,
  output out_12,
  output out_13,
  output out_14
);

  wire converse_1_r_1, converse_1_r_2, converse_1_r_3, converse_1_r_4, converse_2_r_1, converse_2_r_2,
       converse_2_r_3, converse_2_r_4, summator8bit_1_out_21, summator8bit_1_out_22, summator8bit_1_out_23,
       summator8bit_1_out_24, summator8bit_1_s_1, summator8bit_2_out_21, summator8bit_2_out_22,
       summator8bit_2_out_23, summator8bit_2_out_24, summator8bit_2_s_1;

  converse converse_1 (
    .x_4(in_5), .x_3(in_6), .x_2(in_7), .x_1(in_8), .r_4(converse_1_r_4), .r_3(converse_1_r_3),
    .r_2(converse_1_r_2), .r_1(converse_1_r_1));
  converse converse_2 (
    .x_4(in_1), .x_3(in_2), .x_2(in_3), .x_1(in_4), .r_4(converse_2_r_4), .r_3(converse_2_r_3),
    .r_2(converse_2_r_2), .r_1(converse_2_r_1));
  summator8bit summator8bit_1 (
    .x1_8(1'b0), .in_2(1'b0), .in_3(1'b0), .in_4(1'b0), .in_5(converse_1_r_4), .in_6(converse_1_r_3),
    .in_7(converse_1_r_2), .x1_1(converse_1_r_1), .x2_8(1'b0), .in_10(1'b0), .in_11(1'b0), .in_12(1'b0),
    .in_13(converse_2_r_4), .in_14(converse_2_r_3), .in_15(converse_2_r_2), .x2_1(converse_2_r_1),
    .out_21(summator8bit_1_out_21), .out_22(summator8bit_1_out_22), .out_23(summator8bit_1_out_23),
    .out_24(summator8bit_1_out_24), .s_1(summator8bit_1_s_1));  // open: p, s_8, out_19, out_20
  summator8bit summator8bit_2 (
    .x1_8(1'b0), .in_2(1'b0), .in_3(1'b0), .in_4(summator8bit_1_out_21), .in_5(summator8bit_1_out_22),
    .in_6(summator8bit_1_out_23), .in_7(summator8bit_1_out_24), .x1_1(summator8bit_1_s_1), .x2_8(1'b0),
    .in_10(1'b0), .in_11(1'b0), .in_12(1'b0), .in_13(1'b1), .in_14(1'b0), .in_15(1'b0), .x2_1(1'b1),
    .out_21(summator8bit_2_out_21), .out_22(summator8bit_2_out_22), .out_23(summator8bit_2_out_23),
    .out_24(summator8bit_2_out_24), .s_1(summator8bit_2_s_1));  // open: p, s_8, out_19, out_20
  enc enc_1 (
    .S4(summator8bit_2_out_21), .S3(summator8bit_2_out_22), .S2(summator8bit_2_out_23),
    .S1(summator8bit_2_out_24), .S0(summator8bit_2_s_1), .T1(out_9), .T0(out_10), .U3(out_11), .U2(out_12),
    .U1(out_13), .U0(out_14));
endmodule

module enc (
  input  S4,
  input  S3,
  input  S2,
  input  S1,
  input  S0,
  output T1,
  output T0,
  output U3,
  output U2,
  output U1,
  output U0
);

  wire and_1_out, and_2_out, and_3_out, and_4_out, and_5_out, and_6_out, and_7_out, and_8_out, and_9_out,
       and_10_out, and_11_out, and_12_out, and_13_out, and_14_out, and_15_out, and_16_out, and_17_out,
       and_18_out, and_19_out, and_20_out, and_21_out, and_22_out, and_23_out, and_24_out, and_25_out,
       and_26_out, not_1_out, not_2_out, not_3_out, not_4_out, not_5_out;

  not not_1 (not_1_out, S4);
  not not_2 (not_2_out, S3);
  not not_3 (not_3_out, S2);
  not not_4 (not_4_out, S1);
  not not_5 (not_5_out, S0);
  and and_1 (and_1_out, S4, S2);
  and and_2 (and_2_out, S4, S3);
  and and_3 (and_3_out, S4, not_2_out, not_3_out);
  and and_4 (and_4_out, S4, not_2_out, not_4_out, not_5_out);
  and and_5 (and_5_out, not_1_out, S3, S1);
  and and_6 (and_6_out, not_1_out, S3, S2);
  and and_7 (and_7_out, S4, not_2_out, not_3_out, S1);
  and and_8 (and_8_out, not_1_out, S3, not_3_out, not_4_out);
  and and_9 (and_9_out, S4, S3, S2, not_4_out);
  and and_10 (and_10_out, not_1_out, not_2_out, S2);
  and and_11 (and_11_out, S3, not_3_out, not_4_out);
  and and_12 (and_12_out, not_1_out, S2, S1);
  and and_13 (and_13_out, S4, not_3_out);
  and and_14 (and_14_out, not_1_out, not_2_out, not_3_out, S1);
  and and_15 (and_15_out, not_1_out, S2, not_4_out);
  and and_16 (and_16_out, S4, S2, S1);
  and and_17 (and_17_out, S4, S3, S1);
  and and_18 (and_18_out, not_1_out, S3, S2);
  and and_19 (and_19_out, not_1_out, not_2_out, S1, not_5_out);
  and and_20 (and_20_out, not_1_out, S3, S2, not_4_out, not_5_out);
  and and_21 (and_21_out, S3, S1, S0);
  and and_22 (and_22_out, S4, not_2_out, not_3_out, not_4_out, not_5_out);
  and and_23 (and_23_out, S4, S1, S0);
  and and_24 (and_24_out, not_1_out, not_2_out, not_4_out, S0);
  and and_25 (and_25_out, S3, not_3_out, S0);
  and and_26 (and_26_out, S4, S2, S0);
  or or_1 (T1, and_1_out, and_2_out);
  or or_2 (T0, and_3_out, and_4_out, and_5_out, and_6_out);
  or or_3 (U3, and_7_out, and_8_out, and_9_out);
  or or_4 (U2, and_10_out, and_11_out, and_12_out, and_13_out);
  or or_5 (U1, and_14_out, and_15_out, and_16_out, and_17_out, and_18_out);
  or or_6 (U0, and_19_out, and_20_out, and_21_out, and_22_out, and_23_out, and_24_out, and_25_out, and_26_out);
endmodule

module mycounter (
  output Q1,
  output Q2,
  output Q3
);

  wire and_1_out, clock_1_out;

  Clock clock_1 (.out(clock_1_out));
  T_Flip_Flop t_ff_1 (.T(1'b1), .clk(clock_1_out), .Q(Q1));  // open: Qn, reset, preset
  T_Flip_Flop t_ff_2 (.T(Q1), .clk(clock_1_out), .Q(Q2));  // open: Qn, reset, preset
  and and_1 (and_1_out, Q1, Q2);
  T_Flip_Flop t_ff_3 (.T(and_1_out), .clk(clock_1_out), .Q(Q3));  // open: Qn, reset, preset
endmodule
